# Fritzing sketch CanSat (saved by Fritzing 0.9.4)
circuit board: 6.94827cm x 5.45851cm
breadboards: 1

parts:
  Part1 = Arduino Uno (Rev3) - ICSP
  R1 = Temperature Sensor (Thermistor) [thermistor_type=NTC package=THT]
  Part2 = Adafruit BMP280 [part_number="Adafruit #2651"]
  MPX4250AP1 = MPX4250AP pressure sensor [part_number=MPX]
  R2 = Resistor [tolerance=±5% resistance=10 package=THT]
  U1 = GAS_SENSOR [package=mq-3]
  Part3 = Adafruit MicroSD card breakout board [part_number="Adafruit #254"]
  MIRF1 = MIRF [package=mirf]
  VCC1 = Battery block 9V
  JACK1 = 2.1mm Barrel Jack with Terminal Block

nets:
  N1: Part1.A0, R1.pin_1, R2.Pin_0
  N2: Part1.A1, MPX4250AP1.V_out
  N3: Part1.A2, U1.B1
  N4: Part1.A4/SDA, Part2.SDI/SDA
  N5: Part1.A5/SCL, Part2.SCK/SCL
  N6: Part1.ICSP_MISO, Part1.D12/MISO, Part3.DO
  VCC: Part1.5V, R1.pin_0, Part2.VCC, MPX4250AP1.Vs, U1.A1, Part3.VCC, MIRF1.2
  N7: Part1.ICSP_SCK, Part1.D13/SCK, Part3.CLK
  N8: Part1.ICSP_MOSI, Part1.D11_PWM/MOSI, Part3.DI
  GND: Part1.GND, Part2.GND, MPX4250AP1.GND, R2.Pin_1, Part3.GND, MIRF1.1
  N9: Part1.D10_PWM/SS, Part3.CS
  N10: Part1.D0/RX, MIRF1.5
  N11: Part1.D1/TX, MIRF1.4
  N12: VCC1.-, JACK1.NEG
  N13: VCC1.+, JACK1.POS

custom parts:
  Adafruit BMP280: Bosch has stepped up their game with their new BMP280 sensor, an environmental sensor with temperature, barometric pressure that is the next generation upgrade to the BMP085/BMP180/BMP183. This sensor is great for all sorts of weather sensing and can even be used in both I2C and SPI! This precision sensor from Bosch is the best low-cost, precision sensing solution for measuring barometric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
  Adafruit MicroSD card breakout board: Not just a simple breakout board, this microSD adapter goes the extra mile - designed for ease of use. Onboard 5v->3v regulator provides 150mA for power-hungry cards 3v level shifting means you can use this with ease on either 3v or 5v systems Uses a proper level shifting chip, not resistors: less problems, and faster read/write access Use 3 or 4 digital pins to read and write 2Gb+ of storage!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
